// Logisim project 4e3bits.circ as structural Verilog: 1 circuit, main circuit main
module main (
  input  in_1,
  input  in_2,
  input  in_3,
  input  in_4,
  input  in_5,
  input  in_6,
  input  in_7,
  input  in_8,
  input  in_9,
  input  in_10,
  input  in_11,
  input  in_12,
  input  in_13,
  input  in_14
);

  wire and_1_out, and_2_out, and_3_out, and_4_out, and_5_out, and_6_out, not_1_out, not_2_out, not_3_out,
       or_1_out, or_2_out, xnor_1_out, xnor_2_out, xnor_3_out, xnor_4_out, xor_1_out, xor_2_out;

  not not_1 (not_1_out, in_10);
  not not_2 (not_2_out, in_12);
  not not_3 (not_3_out, in_14);
  xnor xnor_1 (xnor_1_out, in_7, in_8);
  and and_1 (and_1_out, in_9, not_1_out);
  xor xor_1 (xor_1_out, in_11, in_12);
  and and_2 (and_2_out, in_11, not_2_out);
  xor xor_2 (xor_2_out, in_13, in_14);
  and and_3 (and_3_out, in_13, not_3_out);
  xnor xnor_2 (xnor_2_out, in_1, in_2);
  xnor xnor_3 (xnor_3_out, in_3, in_4);
  xnor xnor_4 (xnor_4_out, in_5, in_6);
  and and_4 (and_4_out, xnor_2_out, xnor_3_out, xnor_4_out, xnor_1_out);
  and and_5 (and_5_out, and_1_out, xor_1_out);
  LED led_1 (.in(and_4_out));
  or or_1 (or_1_out, and_5_out, and_2_out);
  and and_6 (and_6_out, or_1_out, xor_2_out);
  LED led_2 (.in(or_2_out));
  or or_2 (or_2_out, and_6_out, and_3_out);
endmodule
