// Logisim project ALU.circ as structural Verilog: 1 circuit, main circuit main
module main (
  input  Carry_in,
  input  INVA,
  input  A,
  input  ENA,
  input  B,
  input  ENB,
  input  Carry_in_2,
  input  INVA_2,
  input  A_2,
  input  ENA_2,
  input  B_2,
  input  F0,
  input  ENB_2,
  input  F1,
  input  F0_2,
  input  F1_2
);

  wire and_1_out, and_2_out, and_3_out, and_4_out, and_5_out, and_6_out, and_7_out, and_8_out, and_9_out,
       and_10_out, and_11_out, and_12_out, and_13_out, and_14_out, and_15_out, and_16_out, and_17_out,
       and_18_out, and_19_out, and_20_out, and_21_out, and_22_out, and_23_out, and_24_out, and_25_out,
       and_26_out, not_1_out, not_2_out, not_3_out, not_4_out, not_5_out, not_6_out, not_7_out, not_8_out,
       not_9_out, not_10_out, or_1_out, or_2_out, or_3_out, or_4_out, or_5_out, or_6_out, xor_1_out,
       xor_2_out, xor_3_out, xor_4_out, xor_5_out, xor_6_out;

  and and_1 (and_1_out, A, ENA);
  and and_2 (and_2_out, B, ENB);
  not not_1 (not_1_out, F0);
  xor xor_1 (xor_1_out, INVA, and_1_out);
  not not_2 (not_2_out, F1);
  not not_3 (not_3_out, F0);
  not not_4 (not_4_out, F1);
  and and_3 (and_3_out, not_1_out, not_2_out);
  and and_4 (and_4_out, not_3_out, F1);
  and and_5 (and_5_out, F0, not_4_out);
  and and_6 (and_6_out, F0, F1);
  and and_7 (and_7_out, xor_1_out, and_2_out);
  or or_1 (or_1_out, xor_1_out, and_2_out);
  not not_5 (not_5_out, and_2_out);
  and and_8 (and_8_out, and_6_out, xor_1_out, and_2_out);
  or or_2 (or_2_out, and_8_out, and_12_out);
  LED led_1 (.in(or_2_out));
  and and_9 (and_9_out, and_7_out, and_3_out);
  and and_10 (and_10_out, or_1_out, and_4_out);
  and and_11 (and_11_out, not_5_out, and_5_out);
  xor xor_2 (xor_2_out, and_2_out, xor_1_out);
  and and_12 (and_12_out, and_6_out, xor_2_out, Carry_in);
  xor xor_3 (xor_3_out, Carry_in, xor_2_out);
  and and_13 (and_13_out, xor_3_out, and_6_out);
  LED led_2 (.in(or_3_out));
  or or_3 (or_3_out, and_9_out, and_10_out, and_11_out, and_13_out);
  and and_14 (and_14_out, A_2, ENA_2);
  and and_15 (and_15_out, B_2, ENB_2);
  not not_6 (not_6_out, F0_2);
  xor xor_4 (xor_4_out, INVA_2, and_14_out);
  not not_7 (not_7_out, F1_2);
  not not_8 (not_8_out, F0_2);
  not not_9 (not_9_out, F1_2);
  not not_10 (not_10_out, and_15_out);
  and and_16 (and_16_out, not_6_out, not_7_out);
  and and_17 (and_17_out, not_8_out, F1_2);
  and and_18 (and_18_out, F0_2, not_9_out);
  and and_19 (and_19_out, F0_2, F1_2);
  and and_20 (and_20_out, xor_4_out, and_15_out);
  or or_4 (or_4_out, xor_4_out, and_15_out);
  and and_21 (and_21_out, and_19_out, xor_4_out, and_15_out);
  and and_22 (and_22_out, and_20_out, and_16_out);
  and and_23 (and_23_out, or_4_out, and_17_out);
  and and_24 (and_24_out, not_10_out, and_18_out);
  xor xor_5 (xor_5_out, and_15_out, xor_4_out);
  or or_5 (or_5_out, and_21_out, and_25_out);
  LED led_3 (.in(or_5_out));
  and and_25 (and_25_out, and_19_out, xor_5_out, Carry_in_2);
  xor xor_6 (xor_6_out, Carry_in_2, xor_5_out);
  and and_26 (and_26_out, xor_6_out, and_19_out);
  or or_6 (or_6_out, and_22_out, and_23_out, and_24_out, and_26_out);
  LED led_4 (.in(or_6_out));

  // Notes on the sheet:
  //   AB
  //   A + B
  //   B'
  //   Output
  //   AB
  //   A + B
  //   B'
  //   Carry out
  //   Output
endmodule
