// Logisim project DeslocadorDe1Bit.circ as structural Verilog: 1 circuit, main circuit main
module main (
  input  in_1,
  input  in_2,
  input  in_3,
  input  in_4,
  input  in_5,
  input  in_6,
  input  in_7,
  input  in_8,
  input  in_9
);

  wire and_1_out, and_2_out, and_3_out, and_4_out, and_5_out, and_6_out, and_7_out, and_8_out, and_9_out,
       and_10_out, and_11_out, and_12_out, and_13_out, and_14_out, not_1_out, or_1_out, or_2_out, or_3_out,
       or_4_out, or_5_out, or_6_out;

  not not_1 (not_1_out, in_9);
  and and_1 (and_1_out, in_1, in_9);
  LED led_1 (.in(and_3_out));
  and and_2 (and_2_out, in_2, in_9);
  and and_3 (and_3_out, not_1_out, in_2);
  or or_1 (or_1_out, and_1_out, and_4_out);
  LED led_2 (.in(or_1_out));
  and and_4 (and_4_out, not_1_out, in_3);
  and and_5 (and_5_out, in_3, in_9);
  or or_2 (or_2_out, and_2_out, and_6_out);
  LED led_3 (.in(or_2_out));
  and and_6 (and_6_out, not_1_out, in_4);
  or or_3 (or_3_out, and_5_out, and_9_out);
  LED led_4 (.in(or_3_out));
  and and_7 (and_7_out, in_4, in_9);
  and and_8 (and_8_out, in_5, in_9);
  and and_9 (and_9_out, not_1_out, in_5);
  or or_4 (or_4_out, and_7_out, and_10_out);
  LED led_5 (.in(or_4_out));
  and and_10 (and_10_out, not_1_out, in_6);
  buf and_11 (and_11_out, in_9);  // AND_Gate
  or or_5 (or_5_out, and_8_out, and_12_out);
  LED led_6 (.in(or_5_out));
  and and_12 (and_12_out, not_1_out, in_7);
  or or_6 (or_6_out, and_11_out, and_14_out);
  LED led_7 (.in(or_6_out));
  and and_13 (and_13_out, in_7, in_9);
  buf and_14 (and_14_out, in_8);  // AND_Gate
  LED led_8 (.in(and_13_out));
endmodule
