// Logisim project Multiplexador8bits.circ as structural Verilog: 1 circuit, main circuit main
module main (
  input  D0,
  input  D1,
  input  D2,
  input  D3,
  input  D4,
  input  D5,
  input  D6,
  input  D7,
  input  A,
  input  B,
  input  C
);

  wire and_1_out, and_2_out, and_3_out, and_4_out, and_5_out, and_6_out, and_7_out, and_8_out, not_1_out,
       not_2_out, not_3_out, or_1_out, undriven, undriven_2, undriven_3;

  not not_1 (not_1_out, undriven);
  not not_2 (not_2_out, undriven_3);
  not not_3 (not_3_out, undriven_2);
  and and_1 (and_1_out, D0, not_1_out, not_3_out, not_2_out);
  and and_2 (and_2_out, D1, not_1_out, not_3_out, undriven_3);
  and and_3 (and_3_out, D2, undriven_2);
  and and_4 (and_4_out, D3, not_1_out, undriven_2, undriven_3);
  and and_5 (and_5_out, D4, undriven, not_3_out, not_2_out);
  and and_6 (and_6_out, D5, undriven, not_3_out, undriven_3);
  and and_7 (and_7_out, D6, undriven, undriven_2, not_2_out);
  and and_8 (and_8_out, D7, undriven, undriven_2, undriven_3);
  or or_1 (or_1_out, and_1_out, and_2_out, and_3_out, and_4_out, and_5_out, and_6_out, and_7_out, and_8_out);
  LED led_1 (.in(or_1_out));
endmodule
