// Logisim project SN54-74LS682.circ as structural Verilog: 1 circuit, main circuit main
module main (
  input  in_1,
  input  in_2,
  input  in_3,
  input  in_4,
  input  in_5,
  input  in_6,
  input  in_7,
  input  in_8,
  input  in_9,
  input  in_10,
  input  in_11,
  input  in_12,
  input  in_13,
  input  in_14,
  input  in_15,
  input  in_16
);

  wire and_1_out, and_2_out, and_3_out, and_4_out, and_5_out, and_6_out, and_7_out, and_8_out, nand_1_out,
       nor_1_out, not_1_out, xor_1_out, xor_2_out, xor_3_out, xor_5_out, xor_6_out, xor_7_out, xor_8_out;

  not not_1 (not_1_out, in_1);
  not not_2 (not_1_out, in_2);
  not not_3 (not_1_out, in_3);
  not not_4 (not_1_out, in_4);
  not not_5 (not_1_out, in_5);
  not not_6 (not_1_out, in_6);
  not not_7 (not_1_out, in_7);
  not not_8 (not_1_out, in_8);
  not not_9 (not_1_out, in_9);
  not not_10 (not_1_out, in_10);
  not not_11 (not_1_out, in_11);
  not not_12 (not_1_out, in_12);
  not not_13 (not_1_out, in_13);
  not not_14 (not_1_out, in_14);
  not not_15 (not_1_out, in_15);
  not not_16 (not_1_out, in_16);
  xor xor_1 (xor_1_out, not_1_out, not_1_out);
  xor xor_2 (xor_2_out, not_1_out, not_1_out);
  xor xor_3 (xor_3_out, not_1_out, not_1_out);
  xor xor_4 (xor_3_out, not_1_out, not_1_out);
  xor xor_5 (xor_5_out, not_1_out, not_1_out);
  xor xor_6 (xor_6_out, not_1_out, not_1_out);
  xor xor_7 (xor_7_out, not_1_out, not_1_out);
  xor xor_8 (xor_8_out, not_1_out, not_1_out);
  and and_1 (and_1_out, xor_7_out, xor_6_out, xor_5_out, xor_3_out, xor_3_out, xor_2_out, xor_1_out, not_1_out, ~not_1_out);  // AND_Gate
  and and_2 (and_2_out, xor_6_out, xor_5_out, xor_3_out, xor_3_out, xor_2_out, xor_1_out, not_1_out, ~not_1_out);  // AND_Gate
  and and_3 (and_3_out, xor_5_out, xor_3_out, xor_3_out, xor_2_out, xor_1_out, not_1_out, ~not_1_out);  // AND_Gate
  and and_4 (and_4_out, xor_3_out, xor_3_out, xor_2_out, xor_1_out, not_1_out, ~not_1_out);  // AND_Gate
  and and_5 (and_5_out, xor_3_out, xor_2_out, xor_1_out, not_1_out, ~not_1_out);  // AND_Gate
  and and_6 (and_6_out, xor_2_out, xor_1_out, not_1_out, ~not_1_out);  // AND_Gate
  and and_7 (and_7_out, xor_1_out, not_1_out, ~not_1_out);  // AND_Gate
  and and_8 (and_8_out, not_1_out, ~not_1_out);  // AND_Gate
  nand nand_1 (nand_1_out, xor_1_out, xor_2_out, xor_3_out, xor_3_out, xor_5_out, xor_6_out, xor_7_out, xor_8_out);
  nor nor_1 (nor_1_out, and_1_out, and_2_out, and_3_out, and_4_out, and_5_out, and_6_out, and_7_out, and_8_out);
  LED led_1 (.in(nand_1_out));
  LED led_2 (.in(nor_1_out));
endmodule
