// Logisim project Sim12.circ as structural Verilog: 1 circuit, main circuit main
module main (
  input  in_1,
  input  in_2,
  input  in_3,
  input  in_4,
  input  in_5,
  input  in_6,
  input  in_7,
  input  in_8,
  input  in_9,
  input  in_10,
  input  in_11,
  input  in_12,
  input  in_13,
  input  in_14,
  input  in_15,
  input  in_16,
  input  in_17,
  input  \Simulação_2 ,
  input  in_19,
  input  in_20,
  input  in_21,
  input  in_22,
  input  in_23,
  input  in_24,
  input  in_25,
  input  in_26,
  input  in_27,
  input  in_28,
  input  in_29,
  input  in_30,
  input  in_31,
  input  in_32,
  input  in_33
);

  wire and_1_out, and_2_out, and_3_out, and_4_out, and_5_out, and_6_out, and_7_out, not_1_out, not_2_out,
       not_3_out, not_4_out, not_5_out, not_6_out, or_1_out, or_2_out, or_3_out, or_4_out, or_5_out,
       or_6_out, undriven, undriven_2, undriven_3, undriven_4, xor_1_out, xor_2_out, xor_3_out, xor_4_out;

  not not_1 (not_1_out, in_25);
  and and_1 (and_1_out, in_1, in_3);
  LED led_1 (.in(and_1_out));
  or or_1 (or_1_out, in_9, in_11);
  LED led_2 (.in(or_1_out));
  LED led_3 (.in(xor_1_out));
  xor xor_1 (xor_1_out, in_17, in_19);
  LED led_4 (.in(not_1_out));
  and and_2 (and_2_out, undriven, undriven_2);
  or or_2 (or_2_out, undriven_3, undriven_4);
  and and_3 (and_3_out, in_2, in_5);
  and and_4 (and_4_out, in_10, in_12);
  xor xor_2 (xor_2_out, \Simulação_2 , in_23);
  or or_3 (or_3_out, in_28, in_26);
  or or_4 (or_4_out, and_3_out, and_4_out);
  LED led_5 (.in(or_4_out));
  LED led_6 (.in(and_5_out));
  and and_5 (and_5_out, xor_2_out, or_3_out);
  not not_2 (not_2_out, in_6);
  not not_3 (not_3_out, in_13);
  not not_4 (not_4_out, in_24);
  not not_5 (not_5_out, in_27);
  and and_6 (and_6_out, in_4, not_2_out);
  and and_7 (and_7_out, not_3_out, in_16);
  or or_5 (or_5_out, in_20, not_4_out);
  or or_6 (or_6_out, not_5_out, in_29);
  xor xor_3 (xor_3_out, in_30, in_31);
  xor xor_4 (xor_4_out, in_32, in_33);
  LED led_7 (.in(and_6_out));
  LED led_8 (.in(and_7_out));
  LED led_9 (.in(or_5_out));
  LED led_10 (.in(or_6_out));
  LED led_11 (.in(not_6_out));
  not not_6 (not_6_out, xor_3_out);
  LED led_12 (.in(xor_4_out));
  // NOR_Gate nor_1 is placed but not wired
  // NOR_Gate nor_2 is placed but not wired
  // NOR_Gate nor_3 is placed but not wired
  // NOR_Gate nor_4 is placed but not wired

  // Notes on the sheet:
  //   Simulação 1
  //   Comparadores de 1 BIT
  //   A>B
  //   A<B
endmodule
