// Logisim project SomadorCompletoDe2Bits.circ as structural Verilog: 1 circuit, main circuit main
module main (
  input  A0,
  input  B1,
  input  A1,
  input  B1_2
);

  wire and_1_out, and_2_out, and_3_out, or_1_out, xor_1_out, xor_2_out, xor_3_out;

  and and_1 (and_1_out, A1, B1_2);
  xor xor_1 (xor_1_out, A1, B1_2);
  or or_1 (or_1_out, and_1_out, and_3_out);
  and and_2 (and_2_out, A0, B1);
  and and_3 (and_3_out, xor_1_out, and_2_out);
  xor xor_2 (xor_2_out, A0, B1);
  xor xor_3 (xor_3_out, and_2_out, xor_1_out);
  LED led_1 (.in(xor_3_out));
  LED led_2 (.in(xor_2_out));
  LED led_3 (.in(or_1_out));

  // Notes on the sheet:
  //   Somador de 2 bits
  //   Carry out
  //   S1
  //   S0
endmodule
