// Logisim project SomadorParcialDe1Bit.circ as structural Verilog: 1 circuit, main circuit main
module main (
  input  in_1,
  input  in_2
);

  wire and_1_out, xor_1_out;

  and and_1 (and_1_out, in_1, in_2);
  xor xor_1 (xor_1_out, in_1, in_2);
  LED led_1 (.in(and_1_out));
  LED led_2 (.in(xor_1_out));

  // Notes on the sheet:
  //   Somador parcial(Half Adder) de 1 bit
  //   Carry
  //   Sum
endmodule
