// Logisim project circuitosbasicos.circ as structural Verilog: 1 circuit, main circuit main
module main (
  input  in_1,
  input  in_2,
  input  in_3,
  input  in_4,
  input  in_5,
  input  in_6,
  input  in_7,
  input  A,
  input  A_2,
  input  B,
  input  B_2,
  input  C,
  input  C_2,
  input  D,
  input  D_2,
  input  A_3,
  input  A_4,
  input  A_5,
  input  A_6,
  input  B_3,
  input  B_4,
  input  B_5,
  input  A_7,
  input  A_8,
  input  A_9,
  input  A_10,
  input  A_11,
  input  B_6,
  input  B_7,
  input  B_8,
  input  A_12,
  input  A_13,
  input  A_14,
  input  B_9,
  input  B_10
);

  wire and_1_out, and_2_out, and_3_out, and_4_out, and_5_out, nand_1_out, nand_2_out, nand_3_out, nor_1_out,
       not_1_out, not_2_out, not_3_out, not_4_out, not_5_out, not_6_out, or_1_out, or_2_out, or_3_out,
       or_4_out, undriven, undriven_2, undriven_3, undriven_4, xor_1_out, xor_3_out, xor_4_out;

  not not_1 (not_1_out, B_3);
  not not_2 (not_2_out, B_6);
  and and_1 (and_1_out, in_1, in_3);
  or or_1 (or_1_out, in_5, in_7);
  and and_2 (and_2_out, A, B);
  and and_3 (and_3_out, C, D);
  and and_4 (and_4_out, A_5, not_1_out);
  or or_2 (or_2_out, A_8, not_2_out);
  xor xor_1 (xor_1_out, A_14, B_10);
  LED led_1 (.in(and_1_out));
  LED led_2 (.in(or_1_out));
  LED led_3 (.in(and_4_out));
  LED led_4 (.in(or_2_out));
  LED led_5 (.in(not_3_out));
  not not_3 (not_3_out, xor_1_out);
  nand nand_1 (nand_1_out, and_2_out, and_3_out);
  not not_4 (not_4_out, A_6);
  not not_5 (not_5_out, A_9);
  // XOR_Gate xor_2 has open pins: in0=in_2, in1=in_4, out=open
  not not_6 (not_6_out, in_6);
  LED led_6 (.in(nand_1_out));
  and and_5 (and_5_out, not_4_out, B_4);
  or or_3 (or_3_out, not_5_out, B_7);
  xor xor_3 (xor_3_out, A_13, B_9);
  LED led_7 (.in(not_6_out));
  LED led_8 (.in(and_5_out));
  LED led_9 (.in(or_3_out));
  LED led_10 (.in(xor_3_out));
  xor xor_4 (xor_4_out, A_2, B_2);
  or or_4 (or_4_out, C_2, D_2);
  nand nand_2 (nand_2_out, undriven, undriven_2);
  nor nor_1 (nor_1_out, undriven_3, undriven_4);
  nand nand_3 (nand_3_out, xor_4_out, or_4_out);
  LED led_11 (.in(nand_3_out));

  // Notes on the sheet:
  //   A = B
  //   A > B
  //   A >= B
  //   A < B
  //   A <= B
  //   A != B
endmodule
