// Logisim project comparadores.circ as structural Verilog: 1 circuit, main circuit main
module main (
  input  A0,
  input  B0,
  input  A1,
  input  B1,
  input  A2,
  input  B2,
  input  A3,
  input  B3,
  input  A0_2,
  input  B0_2,
  input  A1_2,
  input  B1_2,
  input  A2_2,
  input  B2_2
);

  wire and_1_out, and_2_out, and_3_out, and_4_out, and_5_out, and_6_out, not_1_out, not_2_out, not_3_out,
       or_1_out, or_2_out, xnor_1_out, xnor_2_out, xnor_3_out, xnor_4_out, xnor_5_out, xnor_6_out;

  not not_1 (not_1_out, B0_2);
  not not_2 (not_2_out, B1_2);
  not not_3 (not_3_out, B2_2);
  xnor xnor_1 (xnor_1_out, A0, B0);
  xnor xnor_2 (xnor_2_out, A1, B1);
  xnor xnor_3 (xnor_3_out, A2, B2);
  xnor xnor_4 (xnor_4_out, A3, B3);
  and and_1 (and_1_out, A0_2, not_1_out);
  xnor xnor_5 (xnor_5_out, A1_2, B1_2);
  and and_2 (and_2_out, A1_2, not_2_out);
  xnor xnor_6 (xnor_6_out, A2_2, B2_2);
  and and_3 (and_3_out, A2_2, not_3_out);
  and and_4 (and_4_out, xnor_1_out, xnor_2_out, xnor_3_out, xnor_4_out);
  and and_5 (and_5_out, and_1_out, xnor_5_out);
  and and_6 (and_6_out, or_1_out, xnor_6_out);
  LED led_1 (.in(and_4_out));
  or or_1 (or_1_out, and_5_out, and_2_out);
  or or_2 (or_2_out, and_6_out, and_3_out);
  LED led_2 (.in(or_2_out));

  // Notes on the sheet:
  //   Comparadores de 4 bits
  //   Comparadores de 3 bits(A > B)
endmodule
