// Logisim project comparadores8bits.circ as structural Verilog: 1 circuit, main circuit main
module main (
  input  A0,
  input  B0,
  input  A0_2,
  input  B0_2,
  input  A1,
  input  B1,
  input  A1_2,
  input  A1_3,
  input  A2,
  input  B2,
  input  A2_2,
  input  A2_3,
  input  A3,
  input  B3,
  input  A3_2,
  input  B3_2,
  input  A4,
  input  B4,
  input  A4_2,
  input  B4_2,
  input  A5,
  input  A5_2,
  input  A5_3,
  input  B5,
  input  A6,
  input  B6,
  input  A6_2,
  input  B6_2,
  input  A7,
  input  B7,
  input  A7_2,
  input  B7_2
);

  wire and_1_out, and_2_out, and_3_out, and_4_out, and_5_out, and_6_out, and_7_out, and_8_out, and_9_out,
       not_1_out, not_2_out, not_3_out, not_4_out, not_5_out, not_6_out, not_7_out, not_8_out, or_1_out,
       xnor_1_out, xnor_2_out, xnor_3_out, xnor_4_out, xnor_5_out, xnor_6_out, xnor_7_out, xnor_8_out;

  not not_1 (not_1_out, B0);
  not not_2 (not_2_out, B1);
  not not_3 (not_3_out, B2);
  not not_4 (not_4_out, B3);
  not not_5 (not_5_out, B4);
  not not_6 (not_6_out, B5);
  not not_7 (not_7_out, B6_2);
  not not_8 (not_8_out, B7_2);
  and and_1 (and_1_out, A0, not_1_out);
  and and_2 (and_2_out, A1, not_2_out);
  and and_3 (and_3_out, A2, not_3_out);
  and and_4 (and_4_out, A3, not_4_out);
  and and_5 (and_5_out, A4, not_5_out);
  and and_6 (and_6_out, A5_3, not_6_out);
  and and_7 (and_7_out, A6_2, not_7_out);
  and and_8 (and_8_out, A7_2, not_8_out);
  or or_1 (or_1_out, and_1_out, and_2_out, and_3_out, and_4_out, and_5_out, and_6_out, and_7_out, and_8_out);
  LED led_1 (.in(or_1_out));
  xnor xnor_1 (xnor_1_out, A0_2, B0_2);
  xnor xnor_2 (xnor_2_out, A1_2, A1_3);
  xnor xnor_3 (xnor_3_out, A2_2, A2_3);
  xnor xnor_4 (xnor_4_out, A3_2, B3_2);
  xnor xnor_5 (xnor_5_out, A4_2, B4_2);
  xnor xnor_6 (xnor_6_out, A5, A5_2);
  xnor xnor_7 (xnor_7_out, A6, B6);
  xnor xnor_8 (xnor_8_out, A7, B7);
  LED led_2 (.in(and_9_out));
  and and_9 (and_9_out, xnor_1_out, xnor_2_out, xnor_3_out, xnor_4_out, xnor_5_out, xnor_6_out, xnor_7_out, xnor_8_out);

  // Notes on the sheet:
  //   Comparadores de 8 bits (A>B)
  //   Comparadores de 8 bits (A>B)
endmodule
