// Logisim project memoriaRam1Bit.circ as structural Verilog: 1 circuit, main circuit main
module main (
  input  Select,
  input  Input,
  input  Read_Write
);

  wire and_1_out, and_2_out, and_3_out, not_1_out, not_2_out, not_3_out, not_4_out, or_1_out, or_2_out;

  not not_1 (not_1_out, Input);
  and and_1 (and_1_out, Select, not_1_out, Read_Write);
  and and_2 (and_2_out, Select, Input, Read_Write);
  or or_1 (or_1_out, and_1_out, not_3_out);
  or or_2 (or_2_out, not_2_out, and_2_out);
  not not_2 (not_2_out, or_1_out);
  not not_3 (not_3_out, or_2_out);
  not not_4 (not_4_out, Read_Write);
  and and_3 (and_3_out, Select, not_2_out, not_4_out);
  LED led_1 (.in(and_3_out));

  // Notes on the sheet:
  //   Memória RAM - Binary Cell (BC)
  //   Output
endmodule
