// Logisim project memoriaRam4x2.circ as structural Verilog: 1 circuit, main circuit main
module main (
  input  D1,
  input  D0,
  input  A0,
  input  A1,
  input  EN,
  input  Read_Write
);

  wire and_1_out, and_2_out, and_3_out, and_4_out, and_5_out, and_6_out, and_7_out, and_8_out, and_9_out,
       and_10_out, and_11_out, and_12_out, and_13_out, and_14_out, and_15_out, and_16_out, and_17_out,
       and_18_out, and_19_out, and_20_out, and_21_out, and_22_out, and_23_out, and_24_out, and_25_out,
       and_26_out, and_27_out, and_28_out, not_1_out, not_2_out, not_3_out, not_4_out, not_5_out, not_6_out,
       not_7_out, not_8_out, not_9_out, not_10_out, not_11_out, not_12_out, not_13_out, not_14_out,
       not_15_out, not_16_out, not_17_out, not_18_out, not_19_out, not_20_out, not_21_out, not_22_out,
       not_23_out, not_24_out, not_25_out, not_26_out, not_27_out, not_28_out, not_29_out, not_30_out,
       not_31_out, not_32_out, not_33_out, not_34_out, or_1_out, or_2_out, or_3_out, or_4_out, or_5_out,
       or_6_out, or_7_out, or_8_out, or_9_out, or_10_out, or_11_out, or_12_out, or_13_out, or_14_out,
       or_15_out, or_16_out, or_17_out, or_18_out;

  not not_1 (not_1_out, A0);
  not not_2 (not_2_out, A1);
  and and_1 (and_1_out, not_1_out, not_2_out, EN);
  and and_2 (and_2_out, A0, not_2_out, EN);
  and and_3 (and_3_out, not_1_out, A1, EN);
  and and_4 (and_4_out, A0, A1, EN);
  not not_3 (not_3_out, D1);
  not not_4 (not_4_out, D1);
  not not_5 (not_5_out, D1);
  not not_6 (not_6_out, D1);
  and and_5 (and_5_out, and_2_out, not_5_out, Read_Write);
  and and_6 (and_6_out, and_2_out, D1, Read_Write);
  and and_7 (and_7_out, and_3_out, not_6_out, Read_Write);
  and and_8 (and_8_out, and_3_out, D1, Read_Write);
  and and_9 (and_9_out, and_4_out, not_3_out, Read_Write);
  and and_10 (and_10_out, and_4_out, D1, Read_Write);
  and and_11 (and_11_out, and_1_out, not_4_out, Read_Write);
  and and_12 (and_12_out, and_1_out, D1, Read_Write);
  or or_1 (or_1_out, and_11_out, not_8_out);
  or or_2 (or_2_out, not_7_out, and_12_out);
  or or_3 (or_3_out, and_5_out, not_10_out);
  or or_4 (or_4_out, not_9_out, and_6_out);
  or or_5 (or_5_out, and_7_out, not_12_out);
  or or_6 (or_6_out, not_11_out, and_8_out);
  or or_7 (or_7_out, and_9_out, not_14_out);
  or or_8 (or_8_out, not_13_out, and_10_out);
  not not_7 (not_7_out, or_1_out);
  not not_8 (not_8_out, or_2_out);
  not not_9 (not_9_out, or_3_out);
  not not_10 (not_10_out, or_4_out);
  not not_11 (not_11_out, or_5_out);
  not not_12 (not_12_out, or_6_out);
  not not_13 (not_13_out, or_7_out);
  not not_14 (not_14_out, or_8_out);
  not not_15 (not_15_out, Read_Write);
  not not_16 (not_16_out, Read_Write);
  not not_17 (not_17_out, Read_Write);
  not not_18 (not_18_out, Read_Write);
  and and_13 (and_13_out, and_4_out, not_13_out, not_18_out);
  and and_14 (and_14_out, and_1_out, not_7_out, not_15_out);
  and and_15 (and_15_out, and_2_out, not_9_out, not_16_out);
  and and_16 (and_16_out, and_3_out, not_11_out, not_17_out);
  or or_9 (or_9_out, and_13_out, and_16_out, and_15_out, and_14_out);
  not not_19 (not_19_out, D0);
  not not_20 (not_20_out, D0);
  not not_21 (not_21_out, D0);
  not not_22 (not_22_out, D0);
  LED led_1 (.in(or_9_out));
  and and_17 (and_17_out, and_2_out, not_21_out, Read_Write);
  and and_18 (and_18_out, and_2_out, D0, Read_Write);
  and and_19 (and_19_out, and_3_out, not_22_out, Read_Write);
  and and_20 (and_20_out, and_3_out, D0, Read_Write);
  and and_21 (and_21_out, and_4_out, not_19_out, Read_Write);
  and and_22 (and_22_out, and_4_out, D0, Read_Write);
  and and_23 (and_23_out, and_1_out, not_20_out, Read_Write);
  and and_24 (and_24_out, and_1_out, D0, Read_Write);
  or or_10 (or_10_out, and_23_out, not_24_out);
  or or_11 (or_11_out, not_23_out, and_24_out);
  or or_12 (or_12_out, and_17_out, not_26_out);
  or or_13 (or_13_out, not_25_out, and_18_out);
  or or_14 (or_14_out, and_19_out, not_28_out);
  or or_15 (or_15_out, not_27_out, and_20_out);
  or or_16 (or_16_out, and_21_out, not_30_out);
  or or_17 (or_17_out, not_29_out, and_22_out);
  LED led_2 (.in(or_18_out));
  not not_23 (not_23_out, or_10_out);
  not not_24 (not_24_out, or_11_out);
  not not_25 (not_25_out, or_12_out);
  not not_26 (not_26_out, or_13_out);
  not not_27 (not_27_out, or_14_out);
  not not_28 (not_28_out, or_15_out);
  not not_29 (not_29_out, or_16_out);
  not not_30 (not_30_out, or_17_out);
  not not_31 (not_31_out, Read_Write);
  not not_32 (not_32_out, Read_Write);
  not not_33 (not_33_out, Read_Write);
  not not_34 (not_34_out, Read_Write);
  and and_25 (and_25_out, and_4_out, not_29_out, not_34_out);
  and and_26 (and_26_out, and_1_out, not_23_out, not_31_out);
  and and_27 (and_27_out, and_2_out, not_25_out, not_32_out);
  and and_28 (and_28_out, and_3_out, not_27_out, not_33_out);
  or or_18 (or_18_out, and_25_out, and_28_out, and_27_out, and_26_out);

  // Notes on the sheet:
  //   S0
  //   S1
  //   S2
  //   S3
  //   Input
  //   Z0
  //   Outputs
  //   Z1
endmodule
